// Logisim project Circuit.circ as structural Verilog: 4 circuits, main circuit main
module main (
);

  wire clock_1_out, main_cpu_ram_load, por_1_out, ram_slot_1_ram_clock_out, ram_slot_1_ram_load_out,
       ram_slot_1_ram_store_out;
  wire [15:0] main_cpu_ram_addr, main_ram_dout, ram_slot_1_ram_addr_out, ram_slot_1_ram_data_out,
       ram_slot_1_ram_value_out;

  POR #(.PorHighDuration(1)) por_1 (.out(por_1_out));
  Clock clock_1 (.out(clock_1_out));
  ram_slot ram_slot_1 (
    .RAM_LOAD_IN(main_cpu_ram_load), .RAM_CLOCK_IN(clock_1_out), .RAM_ADDR_IN(main_cpu_ram_addr),
    .RAM_DATA_IN(main_ram_dout), .RAM_ADDR_OUT(ram_slot_1_ram_addr_out),
    .RAM_VALUE_OUT(ram_slot_1_ram_value_out), .RAM_DATA_OUT(ram_slot_1_ram_data_out),
    .RAM_LOAD_OUT(ram_slot_1_ram_load_out), .RAM_STORE_OUT(ram_slot_1_ram_store_out),
    .RAM_CLOCK_OUT(ram_slot_1_ram_clock_out));  // open: RAM_STORE_IN, RAM_VALUE_IN
  RAM #(.addrWidth(16), .dataWidth(16)) main_ram (
    .addr(ram_slot_1_ram_addr_out), .we(ram_slot_1_ram_store_out), .oe(ram_slot_1_ram_load_out),
    .clk(ram_slot_1_ram_clock_out), .din(ram_slot_1_ram_value_out), .dout(main_ram_dout));
  cpu main_cpu (
    .RESET(por_1_out), .CLOCK(clock_1_out), .RAM_OUT(ram_slot_1_ram_data_out), .RAM_ADDR(main_cpu_ram_addr),
    .RAM_LOAD(main_cpu_ram_load));
endmodule

module cpu (
  input  RESET,
  input  CLOCK,
  input  [15:0] RAM_OUT,
  output [15:0] RAM_ADDR,
  output RAM_LOAD
);

  wire demultiplexer_1_out0, demultiplexer_1_out1, demultiplexer_1_out2, demultiplexer_1_out3,
       demultiplexer_1_out4, demultiplexer_1_out5, demultiplexer_1_out6, demultiplexer_1_out7,
       demultiplexer_2_out0, demultiplexer_2_out1, demultiplexer_2_out2, demultiplexer_2_out3,
       demultiplexer_2_out4, demultiplexer_2_out5, demultiplexer_2_out6, demultiplexer_2_out7,
       demultiplexer_2_out8, demultiplexer_2_out9, demultiplexer_2_out10, demultiplexer_2_out11,
       demultiplexer_2_out12, demultiplexer_2_out13, demultiplexer_2_out14, demultiplexer_2_out15, or_1_out,
       or_2_out, or_3_out, or_4_out, or_5_out, or_6_out, or_7_out, or_8_out, or_9_out, or_10_out, or_11_out,
       or_12_out, or_13_out, or_14_out, or_15_out, or_16_out, r8_write, r16_write, RESET_t, STAGE_EXE1,
       STAGE_EXE2, STAGE_LOAD, undriven_2, undriven_3;
  wire [7:0] mux8x_value, mux8y_value;
  wire [15:0] cur_instr, ProgramCounter_q, register_2_q, register_4_q, register_6_q, register_8_q,
       register_10_q, register_12_q, register_14_q, register_16_q, undriven;

  pull pull_1 (.pull_in({r16_write, undriven_2}));
  Demultiplexer #(.select(3)) demultiplexer_1 (
    .out0(demultiplexer_1_out0), .out1(demultiplexer_1_out1), .out2(demultiplexer_1_out2),
    .out3(demultiplexer_1_out3), .out4(demultiplexer_1_out4), .out5(demultiplexer_1_out5),
    .out6(demultiplexer_1_out6), .out7(demultiplexer_1_out7), .in(undriven_2), .sel(cur_instr[2:0]));
  pull pull_2 (.pull_in({r8_write, undriven_3}));
  Demultiplexer #(.select(4)) demultiplexer_2 (
    .out0(demultiplexer_2_out0), .out1(demultiplexer_2_out1), .out2(demultiplexer_2_out2),
    .out3(demultiplexer_2_out3), .out4(demultiplexer_2_out4), .out5(demultiplexer_2_out5),
    .out6(demultiplexer_2_out6), .out7(demultiplexer_2_out7), .out8(demultiplexer_2_out8),
    .out9(demultiplexer_2_out9), .out10(demultiplexer_2_out10), .out11(demultiplexer_2_out11),
    .out12(demultiplexer_2_out12), .out13(demultiplexer_2_out13), .out14(demultiplexer_2_out14),
    .out15(demultiplexer_2_out15), .in(undriven_3), .sel(cur_instr[3:0]));
  Counter #(.max('hffff), .width(16)) ProgramCounter (
    .clr(RESET), .count(STAGE_LOAD), .clk(CLOCK), .Q(ProgramCounter_q));  // open: load, up, D, carry
  D_Flip_Flop #(.trigger("falling")) d_ff_1 (
    .D(STAGE_EXE2), .clk(CLOCK), .Q(STAGE_LOAD), .preset(RESET));  // open: Qn, reset
  D_Flip_Flop #(.trigger("falling")) d_ff_2 (
    .D(STAGE_LOAD), .clk(CLOCK), .Q(STAGE_EXE1), .reset(RESET));  // open: Qn, preset
  D_Flip_Flop #(.trigger("falling")) d_ff_3 (
    .D(STAGE_EXE1), .clk(CLOCK), .Q(STAGE_EXE2), .reset(RESET));  // open: Qn, preset
  assign RAM_LOAD = STAGE_LOAD ? STAGE_LOAD : 1'bz;  // Controlled_Buffer controlled_buffer_1
  assign RAM_ADDR = STAGE_LOAD ? ProgramCounter_q : 16'bz;  // Controlled_Buffer controlled_buffer_2
  or or_1 (or_1_out, demultiplexer_1_out0, demultiplexer_2_out0);
  or or_2 (or_2_out, demultiplexer_1_out0, demultiplexer_2_out1);
  or or_3 (or_3_out, demultiplexer_1_out1, demultiplexer_2_out2);
  or or_4 (or_4_out, demultiplexer_1_out1, demultiplexer_2_out3);
  or or_5 (or_5_out, demultiplexer_1_out2, demultiplexer_2_out4);
  or or_6 (or_6_out, demultiplexer_1_out2, demultiplexer_2_out5);
  or or_7 (or_7_out, demultiplexer_1_out3, demultiplexer_2_out6);
  or or_8 (or_8_out, demultiplexer_1_out3, demultiplexer_2_out7);
  or or_9 (or_9_out, demultiplexer_1_out4, demultiplexer_2_out8);
  or or_10 (or_10_out, demultiplexer_1_out4, demultiplexer_2_out9);
  or or_11 (or_11_out, demultiplexer_1_out5, demultiplexer_2_out10);
  or or_12 (or_12_out, demultiplexer_1_out5, demultiplexer_2_out11);
  or or_13 (or_13_out, demultiplexer_1_out6, demultiplexer_2_out12);
  or or_14 (or_14_out, demultiplexer_1_out6, demultiplexer_2_out13);
  or or_15 (or_15_out, demultiplexer_1_out7, demultiplexer_2_out14);
  or or_16 (or_16_out, demultiplexer_1_out7, demultiplexer_2_out15);
  Register #(.width(16)) CurInstr (.D(RAM_OUT), .en(STAGE_LOAD), .clk(CLOCK), .Q(cur_instr), .clr(RESET_t));
  Register register_1 (.D(undriven[15:8]), .en(or_1_out), .clk(CLOCK), .Q(register_2_q[15:8]), .clr(RESET));
  Register register_2 (.D(undriven[7:0]), .en(or_2_out), .clk(CLOCK), .Q(register_2_q[7:0]));  // open: clr
  Register register_3 (.D(undriven[15:8]), .en(or_3_out), .clk(CLOCK), .Q(register_4_q[15:8]), .clr(RESET));
  Register register_4 (.en(or_4_out), .clk(CLOCK), .Q(register_4_q[7:0]), .clr(RESET));  // open: D
  Register register_5 (.D(undriven[15:8]), .en(or_5_out), .clk(CLOCK), .Q(register_6_q[15:8]), .clr(RESET));
  Register register_6 (.D(undriven[7:0]), .en(or_6_out), .clk(CLOCK), .Q(register_6_q[7:0]), .clr(RESET));
  Register register_7 (.D(undriven[15:8]), .en(or_7_out), .clk(CLOCK), .Q(register_8_q[15:8]), .clr(RESET));
  Register register_8 (.D(undriven[7:0]), .en(or_8_out), .clk(CLOCK), .Q(register_8_q[7:0]), .clr(RESET));
  Register register_9 (.D(undriven[15:8]), .en(or_9_out), .clk(CLOCK), .Q(register_10_q[15:8]));  // open: clr
  Register register_10 (.D(undriven[7:0]), .en(or_10_out), .clk(CLOCK), .Q(register_10_q[7:0]), .clr(RESET));
  Register register_11 (.D(undriven[15:8]), .en(or_11_out), .clk(CLOCK), .Q(register_12_q[15:8]), .clr(RESET));
  Register register_12 (.D(undriven[7:0]), .en(or_12_out), .clk(CLOCK), .Q(register_12_q[7:0]), .clr(RESET));
  Register register_13 (.D(undriven[15:8]), .en(or_13_out), .clk(CLOCK), .Q(register_14_q[15:8]), .clr(RESET));
  Register register_14 (.D(undriven[7:0]), .en(or_14_out), .clk(CLOCK), .Q(register_14_q[7:0]), .clr(RESET));
  Register register_15 (.D(undriven[15:8]), .en(or_15_out), .clk(CLOCK), .Q(register_16_q[15:8]), .clr(RESET));
  Register register_16 (.D(undriven[7:0]), .en(or_16_out), .clk(CLOCK), .Q(register_16_q[7:0]), .clr(RESET));
  Multiplexer #(.select(3), .width(16)) multiplexer_1 (
    .in0(register_2_q), .in1(register_4_q), .in2(register_6_q), .in3(register_8_q), .in4(register_10_q),
    .in5(register_12_q), .in6(register_14_q), .in7(register_16_q));  // open: out, sel
  Multiplexer #(.select(3), .width(16)) multiplexer_2 (
    .in0(register_2_q), .in1(register_4_q), .in2(register_6_q), .in3(register_8_q), .in4(register_10_q),
    .in5(register_12_q), .in6(register_14_q), .in7(register_16_q));  // open: out, sel
  Multiplexer #(.select(4), .width(8)) multiplexer_3 (
    .in0(register_2_q[15:8]), .in1(register_2_q[7:0]), .in2(register_4_q[15:8]), .in3(register_4_q[7:0]),
    .in4(register_6_q[15:8]), .in5(register_6_q[7:0]), .in6(register_8_q[15:8]), .in7(register_8_q[7:0]),
    .in8(register_10_q[15:8]), .in9(register_10_q[7:0]), .in10(register_12_q[15:8]),
    .in11(register_12_q[7:0]), .in12(register_14_q[15:8]), .in13(register_14_q[7:0]),
    .in14(register_16_q[15:8]), .in15(register_16_q[7:0]), .out(mux8x_value), .sel(cur_instr[11:8]));
  Multiplexer #(.select(4), .width(8)) multiplexer_4 (
    .in0(register_2_q[15:8]), .in1(register_2_q[7:0]), .in2(register_4_q[15:8]), .in3(register_4_q[7:0]),
    .in4(register_6_q[15:8]), .in5(register_6_q[7:0]), .in6(register_8_q[15:8]), .in7(register_8_q[7:0]),
    .in8(register_10_q[15:8]), .in9(register_10_q[7:0]), .in10(register_12_q[15:8]),
    .in11(register_12_q[7:0]), .in12(register_14_q[15:8]), .in13(register_14_q[7:0]),
    .in14(register_16_q[15:8]), .in15(register_16_q[7:0]), .out(mux8y_value), .sel(cur_instr[11:8]));

  // Other names for the same wires on the sheet: mux8w[3:0] = cur_instr[3:0]; mux16w[2:0] = cur_instr[2:0];
  //   mux16y[2:0] = cur_instr[5:3]; mux8y[3:0] = cur_instr[7:4]; op_value8[7:0] = cur_instr[11:4];
  //   mux16x[2:0] = cur_instr[8:6]; mux8x[3:0] = cur_instr[11:8]; op16_sub[3:0] = cur_instr[15:12];
  //   opcode[3:0] = cur_instr[15:12]

  // Notes on the sheet:
  //   INPUTS
  //   pipeline thing
  //   Program Counter
  //   Registers, r1-16
  //   8 bit but can be combined
endmodule

module ram_slot (
  input  [15:0] RAM_ADDR_IN,
  input  [15:0] RAM_VALUE_IN,
  input  [15:0] RAM_DATA_IN,
  input  RAM_LOAD_IN,
  input  RAM_STORE_IN,
  input  RAM_CLOCK_IN,
  output [15:0] RAM_ADDR_OUT,
  output [15:0] RAM_VALUE_OUT,
  output [15:0] RAM_DATA_OUT,
  output RAM_LOAD_OUT,
  output RAM_STORE_OUT,
  output RAM_CLOCK_OUT
);


  assign RAM_ADDR_OUT = RAM_ADDR_IN;
  assign RAM_CLOCK_OUT = RAM_CLOCK_IN;
  assign RAM_DATA_OUT = RAM_DATA_IN;
  assign RAM_LOAD_OUT = RAM_LOAD_IN;
  assign RAM_STORE_OUT = RAM_STORE_IN;
  assign RAM_VALUE_OUT = RAM_VALUE_IN;
endmodule

module pull (
  input  pull_in,
  output pull_out
);


  assign pull_out = pull_in;
endmodule
